// Logisim project jy作业(1)(1).circ as structural Verilog: 15 circuits, main circuit FA4
module main (
  input  Reset
);

  wire alu_1_zero, CLK_out, control_1_out_3, control_1_out_4, control_1_out_5, control_1_out_6,
       control_1_out_7, control_1_out_8, control_1_out_9, control_1_out_10;
  wire [2:0] control_1_out_11;
  wire [4:0] multiplexer_1_out;
  wire [5:0] rom_1_data_2;
  wire [25:0] rom_1_data;
  wire [31:0] alu_1_out, extend_1_lmm32, multiplexer_2_out, multiplexer_3_out, npc_1_pc, ram_1_data,
       register_files_1_a, register_files_1_b;

  Clock CLK (.out(CLK_out));
  control control_1 (
    .in_1(rom_1_data_2), .in_2(rom_1_data[5:0]), .out_3(control_1_out_3), .out_4(control_1_out_4),
    .out_5(control_1_out_5), .out_6(control_1_out_6), .out_7(control_1_out_7), .out_8(control_1_out_8),
    .out_9(control_1_out_9), .out_10(control_1_out_10), .out_11(control_1_out_11));
  Multiplexer #(.width(5), .enable("false")) multiplexer_1 (
    .in0(rom_1_data[20:16]), .in1(rom_1_data[15:11]), .out(multiplexer_1_out), .sel(control_1_out_3));
  Register_Files register_files_1 (
    .W(multiplexer_3_out), .ReWrite(control_1_out_6), .Reset(Reset), .CLK(CLK_out), .RW(multiplexer_1_out),
    .A(register_files_1_a), .B(register_files_1_b), .Ra(rom_1_data[25:21]), .Rb(rom_1_data[20:16]));
  Extend extend_1 (.lmm16(rom_1_data[15:0]), .lmm32(extend_1_lmm32), .Extop(control_1_out_10));
  Multiplexer #(.width(32), .enable("false")) multiplexer_2 (
    .in0(register_files_1_b), .in1(extend_1_lmm32), .out(multiplexer_2_out), .sel(control_1_out_4));
  NPC npc_1 (
    .CLK(CLK_out), .Reset(Reset), .Jump(control_1_out_9), .Branch(control_1_out_8), .Zero(alu_1_zero),
    .lmm32(extend_1_lmm32), .lmm26(rom_1_data), .PC(npc_1_pc));
  ALU alu_1 (
    .ALUctr(control_1_out_11), .Zero(alu_1_zero), .A_31_0(register_files_1_a), .B_31_0(multiplexer_2_out),
    .OUT(alu_1_out));
  ROM #(.addrWidth(24), .dataWidth(32)) rom_1 (.addr(npc_1_pc[25:2]), .data({rom_1_data_2, rom_1_data}), .sel(1'b1));
  RAM #(.dataWidth(32), .bus("separate")) ram_1 (
    .addr(alu_1_out[9:2]), .din(register_files_1_b), .data(ram_1_data), .str(control_1_out_7), .sel(1'b1),
    .clk(CLK_out), .ld(1'b1), .clr(Reset));
  Multiplexer #(.width(32), .enable("false")) multiplexer_3 (
    .in0(alu_1_out), .in1(ram_1_data), .out(multiplexer_3_out), .sel(control_1_out_5));

  // Notes on the sheet:
  //   Instruction memory
  //   Data memory
  //   contents of rom_1 (hex, n*v repeats v):
  //   34010001 211020 221824 222025 64282a c53022 ac060004 8c070004 10c70002 8000000 8000000 8000000
endmodule

module FA1 (
  input  A,
  input  B,
  input  Cin,
  output S,
  output Cout
);

  wire and_1_out, and_2_out, and_3_out, xor_1_out;

  and and_1 (and_1_out, A, B);
  and and_2 (and_2_out, A, Cin);
  and and_3 (and_3_out, B, Cin);
  xor xor_1 (xor_1_out, A, B);
  xor xor_2 (S, xor_1_out, Cin);
  or or_1 (Cout, and_1_out, and_2_out, and_3_out);
endmodule

module FA4 (
  input  in_1,
  input  [3:0] in_2,
  input  [3:0] in_3,
  output [3:0] out_4,
  output out_5
);

  wire fa1_1_cout, fa1_2_cout, fa1_3_cout;

  FA1 fa1_1 (.A(in_2[0]), .B(in_3[0]), .Cin(in_1), .S(out_4[0]), .Cout(fa1_1_cout));
  FA1 fa1_2 (.A(in_2[1]), .B(in_3[1]), .Cin(fa1_1_cout), .S(out_4[1]), .Cout(fa1_2_cout));
  FA1 fa1_3 (.A(in_2[2]), .B(in_3[2]), .Cin(fa1_2_cout), .S(out_4[2]), .Cout(fa1_3_cout));
  FA1 fa1_4 (.A(in_2[3]), .B(in_3[3]), .Cin(fa1_3_cout), .S(out_4[3]), .Cout(out_5));
endmodule

module FA16 (
  input  in_1,
  input  [15:0] in_2,
  input  [15:0] in_3,
  output [15:0] out_4,
  output out_5
);

  wire fa4_1_out_5, fa4_2_out_5, fa4_3_out_5;

  FA4 fa4_1 (.in_2(in_2[3:0]), .in_3(in_3[3:0]), .out_4(out_4[3:0]), .in_1(in_1), .out_5(fa4_1_out_5));
  FA4 fa4_2 (.in_2(in_2[7:4]), .in_3(in_3[7:4]), .out_4(out_4[7:4]), .in_1(fa4_1_out_5), .out_5(fa4_2_out_5));
  FA4 fa4_3 (.in_2(in_2[11:8]), .in_3(in_3[11:8]), .out_4(out_4[11:8]), .in_1(fa4_2_out_5), .out_5(fa4_3_out_5));
  FA4 fa4_4 (.in_2(in_2[15:12]), .in_3(in_3[15:12]), .out_4(out_4[15:12]), .in_1(fa4_3_out_5), .out_5(out_5));
endmodule

module F32 (
  input  in_1,
  input  [31:0] in_2,
  input  [31:0] in_3,
  output [31:0] out_4,
  output out_5
);

  wire fa16_1_out_5;

  FA16 fa16_1 (.in_2(in_2[15:0]), .in_3(in_2[31:16]), .out_4(out_4[15:0]), .in_1(in_1), .out_5(fa16_1_out_5));
  FA16 fa16_2 (.in_2(in_3[15:0]), .in_3(in_3[31:16]), .out_4(out_4[31:16]), .in_1(fa16_1_out_5), .out_5(out_5));
endmodule

module Main_ctr (
  input  [5:0] OP,
  output RegDst,
  output ALUSrc,
  output MemetoReg,
  output RegWrite,
  output MemWrite,
  output Branch,
  output Jump,
  output Extop,
  output [2:0] ALUop
);

  wire and_1_out, and_2_out, and_3_out, not_2_out, not_3_out, not_4_out, not_5_out, not_6_out, not_7_out,
       not_8_out, not_9_out, not_10_out, not_11_out, not_12_out;

  not not_1 (RegDst, OP[0]);
  not not_2 (not_2_out, OP[2]);
  not not_3 (not_3_out, OP[1]);
  not not_4 (not_4_out, OP[1]);
  not not_5 (not_5_out, OP[3]);
  not not_6 (not_6_out, OP[2]);
  not not_7 (not_7_out, OP[3]);
  not not_8 (not_8_out, OP[0]);
  not not_9 (not_9_out, OP[3]);
  not not_10 (not_10_out, OP[2]);
  not not_11 (not_11_out, OP[2]);
  not not_12 (not_12_out, OP[1]);
  not not_13 (ALUop[1], OP[1]);
  not not_14 (ALUop[0], OP[0]);
  and and_1 (and_1_out, not_2_out, not_3_out);
  and and_2 (and_2_out, OP[3], not_4_out);
  and and_3 (and_3_out, OP[5], not_5_out);
  and and_4 (MemWrite, OP[3], not_6_out);
  and and_5 (Branch, not_7_out, OP[2]);
  and and_6 (Jump, OP[1], not_8_out);
  or or_1 (Extop, not_9_out, not_10_out);
  and and_7 (ALUop[2], not_11_out, not_12_out);
  or or_2 (RegWrite, and_1_out, and_2_out, and_3_out);

  assign ALUSrc = OP[0];
  assign MemetoReg = OP[1];
endmodule

module ALU_ctr (
  input  [3:0] funct,
  input  [2:0] ALUop,
  output [2:0] ALUctr
);

  wire and_1_out, and_2_out, and_3_out, and_4_out, and_5_out, and_6_out, and_7_out, and_8_out, not_1_out,
       not_2_out, not_3_out, not_4_out, not_5_out, not_6_out, not_7_out;

  not not_1 (not_1_out, ALUop[2]);
  not not_2 (not_2_out, ALUop[2]);
  not not_3 (not_3_out, ALUop[1]);
  not not_4 (not_4_out, ALUop[2]);
  not not_5 (not_5_out, funct[2]);
  not not_6 (not_6_out, ALUop[2]);
  not not_7 (not_7_out, ALUop[0]);
  and and_1 (and_1_out, not_1_out, ALUop[0]);
  and and_2 (and_2_out, funct[1], ALUop[2]);
  and and_3 (and_3_out, not_2_out, not_3_out);
  and and_4 (and_4_out, not_4_out, ALUop[0]);
  and and_5 (and_5_out, not_5_out, ALUop[2]);
  and and_6 (and_6_out, not_6_out, ALUop[1], not_7_out);
  and and_7 (and_7_out, funct[0], ALUop[2]);
  and and_8 (and_8_out, funct[3], ALUop[2]);
  or or_1 (ALUctr[2], and_1_out, and_2_out);
  or or_2 (ALUctr[1], and_3_out, and_4_out, and_5_out);
  or or_3 (ALUctr[0], and_6_out, and_7_out, and_8_out);
endmodule

module NPC (
  input  CLK,
  input  Reset,
  input  Jump,
  input  Branch,
  input  Zero,
  input  [31:0] lmm32,
  input  [25:0] lmm26,
  output [31:0] PC
);

  wire and_1_out;
  wire [31:0] adder_1_out, adder_2_out, multiplexer_1_out, multiplexer_2_out;

  Register #(.width(32)) register_1 (.D(multiplexer_1_out), .en(1'b1), .Q(PC), .clk(CLK), .clr(Reset));
  Adder #(.width(32)) adder_1 (.a(32'h4), .b(PC), .out(adder_1_out), .cin(1'b0));  // open: cout
  Adder #(.width(32)) adder_2 (.a(adder_1_out), .b({lmm32[29:0], 2'b00}), .out(adder_2_out), .cin(1'b0));  // open: cout
  Multiplexer #(.width(32), .enable("false")) multiplexer_1 (
    .in0(multiplexer_2_out), .in1({adder_1_out[31:28], lmm26, 2'b00}), .out(multiplexer_1_out), .sel(Jump));
  Multiplexer #(.width(32), .enable("false")) multiplexer_2 (
    .in0(adder_1_out), .in1(adder_2_out), .out(multiplexer_2_out), .sel(and_1_out));
  and and_1 (and_1_out, Branch, Zero);
endmodule

module Instruction_Memory (
);

  ROM #(.addrWidth(24), .dataWidth(32)) rom_1 (.sel(1'b1));  // open: addr, data
endmodule

module Register_Files (
  input  [31:0] W,
  input  ReWrite,
  input  Reset,
  input  CLK,
  input  [4:0] Ra,
  input  [4:0] RW,
  input  [4:0] Rb,
  output [31:0] A,
  output [31:0] B
);

  wire and_1_out, and_2_out, and_3_out, and_4_out, and_5_out, and_6_out, and_7_out, and_8_out, and_9_out,
       and_10_out, and_11_out, and_12_out, and_13_out, and_14_out, and_15_out, and_16_out, and_17_out,
       and_18_out, and_19_out, and_20_out, and_21_out, and_22_out, and_23_out, and_24_out, and_25_out,
       and_26_out, and_27_out, and_28_out, and_29_out, and_30_out, and_31_out, and_32_out;
  wire [7:0] decoder_1_out0, decoder_1_out8, decoder_1_out16, decoder_1_out24;
  wire [31:0] R_2_q, R_3_q, R_4_q, R_5_q, R_6_q, R_7_q, R_8_q, R_9_q, R_10_q, R_11_q, R_12_q, R_13_q, R_14_q,
       R_15_q, R_16_q, R_17_q, R_18_q, R_19_q, R_20_q, R_21_q, R_22_q, R_23_q, R_24_q, R_25_q, R_26_q,
       R_27_q, R_28_q, R_29_q, R_30_q, R_31_q, R_32_q, R_q;

  Decoder #(.select(5), .enable("false")) decoder_1 (
    .out0(decoder_1_out0[0]), .out1(decoder_1_out0[1]), .out2(decoder_1_out0[2]), .out3(decoder_1_out0[3]),
    .out4(decoder_1_out0[4]), .out5(decoder_1_out0[5]), .out6(decoder_1_out0[6]), .out7(decoder_1_out0[7]),
    .out8(decoder_1_out8[0]), .out9(decoder_1_out8[1]), .out10(decoder_1_out8[2]), .out11(decoder_1_out8[3]),
    .out12(decoder_1_out8[4]), .out13(decoder_1_out8[5]), .out14(decoder_1_out8[6]),
    .out15(decoder_1_out8[7]), .out16(decoder_1_out16[0]), .out17(decoder_1_out16[1]),
    .out18(decoder_1_out16[2]), .out19(decoder_1_out16[3]), .out20(decoder_1_out16[4]),
    .out21(decoder_1_out16[5]), .out22(decoder_1_out16[6]), .out23(decoder_1_out16[7]),
    .out24(decoder_1_out24[0]), .out25(decoder_1_out24[1]), .out26(decoder_1_out24[2]),
    .out27(decoder_1_out24[3]), .out28(decoder_1_out24[4]), .out29(decoder_1_out24[5]),
    .out30(decoder_1_out24[6]), .out31(decoder_1_out24[7]), .sel(RW));
  and and_1 (and_1_out, ReWrite, decoder_1_out0[7]);
  and and_2 (and_2_out, ReWrite, decoder_1_out8[7]);
  and and_3 (and_3_out, ReWrite, decoder_1_out16[7]);
  and and_4 (and_4_out, ReWrite, decoder_1_out24[7]);
  Register #(.width(32)) R (.D(W), .en(and_1_out), .Q(R_q), .clk(CLK), .clr(Reset));
  Register #(.width(32)) R_2 (.D(W), .en(and_2_out), .Q(R_2_q), .clk(CLK), .clr(Reset));
  Register #(.width(32)) R_3 (.D(W), .en(and_3_out), .Q(R_3_q), .clk(CLK), .clr(Reset));
  Register #(.width(32)) R_4 (.D(W), .en(and_4_out), .Q(R_4_q), .clk(CLK), .clr(Reset));
  Register #(.width(32)) R_5 (.D(W), .en(and_5_out), .Q(R_5_q), .clk(CLK), .clr(Reset));
  and and_5 (and_5_out, ReWrite, decoder_1_out0[6]);
  and and_6 (and_6_out, ReWrite, decoder_1_out8[6]);
  and and_7 (and_7_out, ReWrite, decoder_1_out16[6]);
  and and_8 (and_8_out, ReWrite, decoder_1_out24[6]);
  and and_9 (and_9_out, ReWrite, decoder_1_out0[5]);
  Register #(.width(32)) R_6 (.D(W), .en(and_6_out), .Q(R_6_q), .clk(CLK), .clr(Reset));
  and and_10 (and_10_out, ReWrite, decoder_1_out8[5]);
  Register #(.width(32)) R_7 (.D(W), .en(and_7_out), .Q(R_7_q), .clk(CLK), .clr(Reset));
  and and_11 (and_11_out, ReWrite, decoder_1_out16[5]);
  Register #(.width(32)) R_8 (.D(W), .en(and_8_out), .Q(R_8_q), .clk(CLK), .clr(Reset));
  Register #(.width(32)) R_9 (.D(W), .en(and_9_out), .Q(R_9_q), .clk(CLK), .clr(Reset));
  Register #(.width(32)) R_10 (.D(W), .en(and_10_out), .Q(R_10_q), .clk(CLK), .clr(Reset));
  Register #(.width(32)) R_11 (.D(W), .en(and_11_out), .Q(R_11_q), .clk(CLK), .clr(Reset));
  Register #(.width(32)) R_12 (.D(W), .en(and_12_out), .Q(R_12_q), .clk(CLK), .clr(Reset));
  and and_12 (and_12_out, ReWrite, decoder_1_out24[5]);
  Register #(.width(32)) R_13 (.D(W), .en(and_13_out), .Q(R_13_q), .clk(CLK), .clr(Reset));
  and and_13 (and_13_out, ReWrite, decoder_1_out0[4]);
  and and_14 (and_14_out, ReWrite, decoder_1_out8[4]);
  and and_15 (and_15_out, ReWrite, decoder_1_out16[4]);
  and and_16 (and_16_out, ReWrite, decoder_1_out24[4]);
  and and_17 (and_17_out, ReWrite, decoder_1_out0[3]);
  Register #(.width(32)) R_14 (.D(W), .en(and_14_out), .Q(R_14_q), .clk(CLK), .clr(Reset));
  Register #(.width(32)) R_15 (.D(W), .en(and_15_out), .Q(R_15_q), .clk(CLK), .clr(Reset));
  Register #(.width(32)) R_16 (.D(W), .en(and_16_out), .Q(R_16_q), .clk(CLK), .clr(Reset));
  Register #(.width(32)) R_17 (.D(W), .en(and_17_out), .Q(R_17_q), .clk(CLK), .clr(Reset));
  Register #(.width(32)) R_18 (.D(W), .en(and_18_out), .Q(R_18_q), .clk(CLK), .clr(Reset));
  and and_18 (and_18_out, ReWrite, decoder_1_out8[3]);
  Register #(.width(32)) R_19 (.D(W), .en(and_19_out), .Q(R_19_q), .clk(CLK), .clr(Reset));
  and and_19 (and_19_out, ReWrite, decoder_1_out16[3]);
  Register #(.width(32)) R_20 (.D(W), .en(and_20_out), .Q(R_20_q), .clk(CLK), .clr(Reset));
  and and_20 (and_20_out, ReWrite, decoder_1_out24[3]);
  and and_21 (and_21_out, ReWrite, decoder_1_out0[2]);
  and and_22 (and_22_out, ReWrite, decoder_1_out8[2]);
  and and_23 (and_23_out, ReWrite, decoder_1_out16[2]);
  and and_24 (and_24_out, ReWrite, decoder_1_out24[2]);
  Register #(.width(32)) R_21 (.D(W), .en(and_21_out), .Q(R_21_q), .clk(CLK), .clr(Reset));
  Register #(.width(32)) R_22 (.D(W), .en(and_22_out), .Q(R_22_q), .clk(CLK), .clr(Reset));
  Register #(.width(32)) R_23 (.D(W), .en(and_23_out), .Q(R_23_q), .clk(CLK), .clr(Reset));
  Register #(.width(32)) R_24 (.D(W), .en(and_24_out), .Q(R_24_q), .clk(CLK), .clr(Reset));
  Register #(.width(32)) R_25 (.D(W), .en(and_25_out), .Q(R_25_q), .clk(CLK), .clr(Reset));
  and and_25 (and_25_out, ReWrite, decoder_1_out0[1]);
  Register #(.width(32)) R_26 (.D(W), .en(and_26_out), .Q(R_26_q), .clk(CLK), .clr(Reset));
  and and_26 (and_26_out, ReWrite, decoder_1_out8[1]);
  Register #(.width(32)) R_27 (.D(W), .en(and_27_out), .Q(R_27_q), .clk(CLK), .clr(Reset));
  and and_27 (and_27_out, ReWrite, decoder_1_out16[1]);
  Register #(.width(32)) R_28 (.D(W), .en(and_28_out), .Q(R_28_q), .clk(CLK), .clr(Reset));
  and and_28 (and_28_out, ReWrite, decoder_1_out24[1]);
  and and_29 (and_29_out, ReWrite, decoder_1_out0[0]);
  and and_30 (and_30_out, ReWrite, decoder_1_out8[0]);
  and and_31 (and_31_out, ReWrite, decoder_1_out16[0]);
  and and_32 (and_32_out, ReWrite, decoder_1_out24[0]);
  Register #(.width(32)) R_29 (.D(W), .en(and_29_out), .Q(R_29_q), .clk(CLK), .clr(Reset));
  Register #(.width(32)) R_30 (.D(W), .en(and_30_out), .Q(R_30_q), .clk(CLK), .clr(Reset));
  Register #(.width(32)) R_31 (.D(W), .en(and_31_out), .Q(R_31_q), .clk(CLK), .clr(Reset));
  Register #(.width(32)) R_32 (.D(W), .en(and_32_out), .Q(R_32_q), .clk(CLK), .clr(Reset));
  Multiplexer #(.select(5), .width(32), .enable("false")) multiplexer_1 (
    .in0(R_29_q), .in1(R_25_q), .in2(R_21_q), .in3(R_17_q), .in4(R_13_q), .in5(R_9_q), .in6(R_5_q),
    .in7(R_q), .in8(R_30_q), .in9(R_26_q), .in10(R_22_q), .in11(R_18_q), .in12(R_14_q), .in13(R_10_q),
    .in14(R_6_q), .in15(R_2_q), .in16(R_31_q), .in17(R_27_q), .in18(R_23_q), .in19(R_19_q), .in20(R_15_q),
    .in21(R_11_q), .in22(R_7_q), .in23(R_3_q), .in24(R_32_q), .in25(R_28_q), .in26(R_24_q), .in27(R_20_q),
    .in28(R_16_q), .in29(R_12_q), .in30(R_8_q), .in31(R_4_q), .out(A), .sel(Ra));
  Multiplexer #(.select(5), .width(32), .enable("false")) multiplexer_2 (
    .in0(R_29_q), .in1(R_25_q), .in2(R_21_q), .in3(R_17_q), .in4(R_13_q), .in5(R_9_q), .in6(R_5_q),
    .in7(R_q), .in8(R_30_q), .in9(R_26_q), .in10(R_22_q), .in11(R_18_q), .in12(R_14_q), .in13(R_10_q),
    .in14(R_6_q), .in15(R_2_q), .in16(R_31_q), .in17(R_27_q), .in18(R_23_q), .in19(R_19_q), .in20(R_15_q),
    .in21(R_11_q), .in22(R_7_q), .in23(R_3_q), .in24(R_32_q), .in25(R_28_q), .in26(R_24_q), .in27(R_20_q),
    .in28(R_16_q), .in29(R_12_q), .in30(R_8_q), .in31(R_4_q), .out(B), .sel(Rb));
endmodule

module Extend (
  input  [15:0] lmm16,
  input  Extop,
  output [31:0] lmm32
);

  wire and_1_out;

  Multiplexer #(.width(32), .enable("false")) multiplexer_1 (
    .in0({{16{1'b0}}, lmm16}), .in1({{16{1'b1}}, lmm16}), .out(lmm32), .sel(and_1_out));
  and and_1 (and_1_out, lmm16[15], Extop);
endmodule

module ALU (
  input  [31:0] A_31_0,
  input  [31:0] B_31_0,
  input  [2:0] ALUctr,
  output [31:0] OUT,
  output Zero
);

  wire [31:0] add_sub_1_s, and_1_out, or_1_out;

  nor nor_1 (Zero, add_sub_1_s[31], add_sub_1_s[30], add_sub_1_s[29], add_sub_1_s[28], add_sub_1_s[27], add_sub_1_s[26], add_sub_1_s[25], add_sub_1_s[24], add_sub_1_s[23], add_sub_1_s[22], add_sub_1_s[21], add_sub_1_s[20], add_sub_1_s[19], add_sub_1_s[18], add_sub_1_s[17], add_sub_1_s[16], add_sub_1_s[15], add_sub_1_s[14], add_sub_1_s[13], add_sub_1_s[12], add_sub_1_s[11], add_sub_1_s[10], add_sub_1_s[9], add_sub_1_s[8], add_sub_1_s[7], add_sub_1_s[6], add_sub_1_s[5], add_sub_1_s[4], add_sub_1_s[3], add_sub_1_s[2], add_sub_1_s[1], add_sub_1_s[0]);
  assign and_1_out = A_31_0 & B_31_0;  // AND_Gate and_1, 32 bits wide
  assign or_1_out = A_31_0 | B_31_0;  // OR_Gate or_1, 32 bits wide
  Multiplexer #(.select(3), .width(32), .enable("false")) multiplexer_1 (
    .in0(and_1_out), .in1(or_1_out), .in2(add_sub_1_s), .in3({32{1'b0}}), .in4({32{1'b0}}), .in5({32{1'b0}}),
    .in6(add_sub_1_s), .in7({{31{1'b0}}, add_sub_1_s[31]}), .out(OUT), .sel(ALUctr));
  ADD_SUB add_sub_1 (.A(A_31_0), .B(B_31_0), .S(add_sub_1_s), .ADD_SUB(ALUctr[2]));
endmodule

module ADD_SUB (
  input  [31:0] A,
  input  [31:0] B,
  input  ADD_SUB,
  output [31:0] S
);

  wire [31:0] adder_1_out, subtractor_1_out;

  Adder #(.width(32)) adder_1 (.a(A), .b(B), .out(adder_1_out));  // open: cin, cout
  Subtractor #(.width(32)) subtractor_1 (.a(A), .b(B), .out(subtractor_1_out));  // open: bin, bout
  Multiplexer #(.width(32), .enable("false")) multiplexer_1 (
    .in0(adder_1_out), .in1(subtractor_1_out), .out(S), .sel(ADD_SUB));
endmodule

module control (
  input  [5:0] in_1,
  input  [5:0] in_2,
  output out_3,
  output out_4,
  output out_5,
  output out_6,
  output out_7,
  output out_8,
  output out_9,
  output out_10,
  output [2:0] out_11
);

  wire [2:0] main_ctr_1_aluop;

  Main_ctr main_ctr_1 (
    .OP(in_1), .RegDst(out_3), .ALUSrc(out_4), .MemetoReg(out_5), .RegWrite(out_6), .MemWrite(out_7),
    .Branch(out_8), .Jump(out_9), .Extop(out_10), .ALUop(main_ctr_1_aluop));
  ALU_ctr alu_ctr_1 (.funct(in_2[3:0]), .ALUop(main_ctr_1_aluop), .ALUctr(out_11));
endmodule

module Data_Memory (
  input  MemWrite,
  input  Reset,
  input  CLK
);

  RAM #(.dataWidth(32), .bus("separate")) ram_1 (
    .str(MemWrite), .sel(1'b1), .clk(CLK), .ld(1'b1), .clr(Reset));  // open: addr, din, data
endmodule
